# Fritzing sketch analogread (saved by Fritzing 0.7.12b)
breadboards: 1

parts:
  Arduino1 = Arduino
  R2 = Photocell (LDR) [package=THT]
  R3 = 10k Ω Resistor [package=THT]

nets:
  N1: Arduino1.+5V, R2.pin_1
  N2: Arduino1.A0, R2.pin_0, R3.Pin_1
