# Fritzing sketch blink (saved by Fritzing 0.7.12b)
breadboards: 1

parts:
  Arduino1 = Arduino
  LED1 = LED - 5mm [color="Red (633nm)" package="5 mm [THT]"]
  R1 = 100 Ω Resistor [package=THT]

nets:
  N1: Arduino1.D13, LED1.anode
  N2: Arduino1.GND, R1.Pin_1
  N3: LED1.cathode, R1.Pin_0
