# Fritzing sketch switch (saved by Fritzing 0.7.12b)
breadboards: 1

parts:
  Arduino1 = Arduino
  R3 = 10k Ω Resistor [package=THT]
  S1 = Pushbutton [package="[SMD]"]

nets:
  N1: Arduino1.D2, R3.Pin_1, S1.Pin_3, S1.Pin_4
  N2: Arduino1.+5V, S1.Pin_1, S1.Pin_2
